# Fritzing sketch speaker schematic (saved by Fritzing 0.9.0b)
breadboards: 1

parts:
  R1 = Rotary Potentiometer (Small) [maximum_resistance=2kΩ package=THT]
  SP1 = SPEAKER [package=pcb_mount_speaker]
  LM386N-1 = LM386 [package=dip08]
  C2 = Ceramic Capacitor [capacitance=47nF package="100 mil [THT, multilayer]"]
  C3 = Electrolytic Capacitor [capacitance=220µF package="100 mil [THT, electrolytic]"]
  R2 = Resistor [tolerance=±5% resistance=10 package=THT]
  R3 = Resistor [tolerance=±5% resistance=47k package=THT]
  R4 = Resistor [tolerance=±5% resistance=10k package=THT]
  C4 = Electrolytic Capacitor [capacitance=10µF package="100 mil [THT, electrolytic]"]

nets:
  GND: R1.leg1, SP1.-, LM386N-1.V-, R2.Pin_0, C4.-
  N1: R1.wiper, LM386N-1.+IN, R4.Pin_0
  N2: R1.leg2, R3.Pin_0
  N3: SP1.+, C3.-
  N4: LM386N-1.-IN, R4.Pin_1, C4.+
  N5: LM386N-1.OUT, C2.1, C3.+
  5V: LM386N-1.V+
  N6: C2.0, R2.Pin_1
  Pin 43 (RD0): R3.Pin_1

custom parts:
  LM386: low voltage audio power amplifier
